# Fritzing sketch pinoutPi (saved by Fritzing 0.9.3b)

parts:
  Raspberry_Pi_2 = Raspberry Pi 3 [part_number=RPI-3-V1.2]
  LED2 = LED - 5mm [color="Red (633nm)" package="5 mm [THT]"]
  LED3 = LEDs [package=led10mm]

nets:
  N1: Raspberry_Pi_2.GIPO26, LED3.C
  N2: Raspberry_Pi_2.GND, LED2.cathode, LED3.A
  N3: Raspberry_Pi_2.GIPO21, LED2.anode
